# Fritzing sketch Mikroprozessortechnik_SimonSays_V1.0 (saved by Fritzing 1.0.4)
breadboards: 1

parts:
  Bauteil1 = Arduino Mega 2560 (Rev3)
  LED1 = LED - 5mm [color="Green (570nm)" current=0.030A package="5 mm [THT]"]
  J1 = Piezo Speaker
  R1 = Resistor [tolerance=±5% resistance=220 power=0.25W package=THT]  # not connected
  LED2 = LED - 5mm [color="Red (635nm)" current=0.030A package="5 mm [THT]"]
  R2 = Resistor [tolerance=±5% resistance=220 power=0.25W package=THT]
  R3 = Resistor [tolerance=±5% resistance=220 power=0.25W package=THT]
  LED3 = LED - 5mm [color="Yellow (595nm)" current=0.030A package="5 mm [THT]"]
  R4 = Resistor [tolerance=±5% resistance=220 power=0.25W package=THT]
  LED4 = LED - 5mm [color="Blue (430nm)" current=30mA package="5 mm [THT]"]
  S1 = Pushbutton [package="[THT]"]
  S2 = Pushbutton [package="[THT]"]
  S3 = Pushbutton [package="[THT]"]
  S4 = Pushbutton [package="[THT]"]

nets:
  N1: Bauteil1.5V, J1.pin1, R2.Pin_0, R3.Pin_0, R4.Pin_0
  N2: Bauteil1.GND, S1.Pin_3, S1.Pin_4, S2.Pin_3, S2.Pin_4, S3.Pin_3, S3.Pin_4, S4.Pin_3, S4.Pin_4
  N3: Bauteil1.D30, LED1.anode
  N4: Bauteil1.D31, LED2.anode
  N5: Bauteil1.D32, LED3.anode
  N6: Bauteil1.D33, LED4.anode
  N7: Bauteil1.D48, J1.pin2
  N8: Bauteil1.D50, S1.Pin_1, S1.Pin_2
  N9: Bauteil1.D51, S2.Pin_1, S2.Pin_2
  N10: Bauteil1.D52, S3.Pin_1, S3.Pin_2
  N11: Bauteil1.D53, S4.Pin_1, S4.Pin_2
  N12: LED2.cathode, R2.Pin_1
  N13: R3.Pin_1, LED3.cathode
  N14: R4.Pin_1, LED4.cathode

notes:
  Version 1.0
