# Fritzing sketch Mikroprozessortechnik_SimonSays_V2.0 (saved by Fritzing 1.0.4)
breadboards: 1

parts:
  Bauteil1 = Arduino Mega 2560 (Rev3)
  LED1 = LED - 5mm [color="Green (570nm)" current=0.030A package="5 mm [THT]"]
  LED2 = LED - 5mm [color="Red (635nm)" current=0.030A package="5 mm [THT]"]
  LED3 = LED - 5mm [color="Yellow (595nm)" current=0.030A package="5 mm [THT]"]
  LED4 = LED - 5mm [color="Blue (430nm)" current=30mA package="5 mm [THT]"]
  S1 = Pushbutton [package="[THT]"]
  S2 = Pushbutton [package="[THT]"]
  S3 = Pushbutton [package="[THT]"]
  S4 = Pushbutton [package="[THT]"]
  RE1 = KY-040 Rotary encoder [package=THT]
  LCM1602_IIC2 = LCM1602 IIC [part_number="LCM1602 IIC" chip_label="LCM1602 IIC" package="DIP (Dual Inline) [THT]"]
  LCD2 = LCD screen
  SP1 = SPEAKER [package=pcb_mount_speaker]
  S5 = Pushbutton [package="[THT]"]

nets:
  N1: Bauteil1.D21/SCL, LCM1602_IIC2.SCL
  N2: Bauteil1.D20/SDA, LCM1602_IIC2.SDA
  N3: Bauteil1.D11_PWM, SP1.-
  N4: Bauteil1.D9_PWM, RE1.DT
  N5: Bauteil1.D8_PWM, RE1.CLK
  VCC: Bauteil1.5V, LED1.cathode, LED2.cathode, LED3.cathode, LED4.cathode, RE1.Vcc, LCM1602_IIC2.VCC, SP1.+
  GND: Bauteil1.GND, S1.Pin_3, S1.Pin_4, S2.Pin_3, S2.Pin_4, S3.Pin_3, S3.Pin_4, S4.Pin_3, S4.Pin_4, RE1.GND, LCM1602_IIC2.GND, S5.Pin_3, S5.Pin_4
  N6: Bauteil1.D3_PWM, LED1.anode
  N7: Bauteil1.D4_PWM, LED2.anode
  N8: Bauteil1.D5_PWM, LED3.anode
  N9: Bauteil1.D6_PWM, LED4.anode
  N10: Bauteil1.D7_PWM, RE1.SW
  N11: Bauteil1.D44, S5.Pin_1, S5.Pin_2
  N12: Bauteil1.D50, S1.Pin_1, S1.Pin_2
  N13: Bauteil1.D51, S2.Pin_1, S2.Pin_2
  N14: Bauteil1.D52, S3.Pin_1, S3.Pin_2
  N15: Bauteil1.D53, S4.Pin_1, S4.Pin_2
  VSS: LCM1602_IIC2.VSS, LCD2.VSS
  VDD: LCM1602_IIC2.VDD, LCD2.VDD
  N16: LCM1602_IIC2.V0, LCD2.V0
  N17: LCM1602_IIC2.RS, LCD2.RS
  N18: LCM1602_IIC2.RW, LCD2.R/W
  N19: LCM1602_IIC2.E, LCD2.E
  N20: LCM1602_IIC2.D0, LCD2.DB0
  N21: LCM1602_IIC2.D1, LCD2.DB1
  N22: LCM1602_IIC2.D2, LCD2.DB2
  N23: LCM1602_IIC2.D3, LCD2.DB3
  N24: LCM1602_IIC2.D4, LCD2.DB4
  N25: LCM1602_IIC2.D5, LCD2.DB5
  N26: LCM1602_IIC2.D6, LCD2.DB6
  N27: LCM1602_IIC2.D7, LCD2.DB7
  N28: LCM1602_IIC2.A, LCD2.LED+
  N29: LCM1602_IIC2.K, LCD2.LED-

notes:
  Version 2.0

custom parts:
  KY-040 Rotary encoder: KY-040 Rotary Encoder with switch on breakout borad from AZ Delivery
  LCM1602 IIC: I2C-Module to use a 1602 or 2004 LCD on with the wire.h libory Serial LCD Modul
